// Logisim project Logisim.circ as structural Verilog: 1 circuit, main circuit main
module main (
  input  A,
  input  B,
  input  C,
  input  D,
  input  E,
  input  F,
  input  A_2,
  input  B_2,
  input  C_2,
  input  D_2,
  input  E_2,
  input  F_2,
  output out_13,
  output out_14
);

  wire and_2_out, and_3_out, and_4_out, not_1_out, not_2_out, not_3_out, not_4_out, not_5_out, not_6_out,
       not_7_out, not_8_out;

  not not_1 (not_1_out, A);
  not not_2 (not_2_out, B);
  not not_3 (not_3_out, C);
  not not_4 (not_4_out, A_2);
  not not_5 (not_5_out, C_2);
  not not_6 (not_6_out, D_2);
  not not_7 (not_7_out, E_2);
  not not_8 (not_8_out, F_2);
  and and_1 (out_13, not_1_out, not_2_out, not_3_out);
  and and_2 (and_2_out, not_4_out, B_2, not_5_out);
  and and_3 (and_3_out, not_4_out, B_2, not_6_out);
  and and_4 (and_4_out, not_4_out, not_7_out, not_8_out);
  or or_1 (out_14, and_2_out, and_3_out, and_4_out);

  // Notes on the sheet:
  //   ~A~B~C
  //   Categoria: 1 
  //   Categoria 2:
  //   ~AB~C + ~AB~D +~AB~E~F
endmodule
